# Fritzing sketch trash_talk (saved by Fritzing 0.9.3b)
breadboards: 1

parts:
  U1 = attiny85 [package=dip]
  DFPlayer_Mini1 = DFPlayer MINI [package="DIP (Dual Inline) [THT]"]
  VCC1 = 4 x AAA Battery Mount
  Part1 = SRF05 Ultrasonic Rangefinder
  SP1 = SPEAKER [package=pcb_mount_speaker]

nets:
  N1: U1.Pin_4, DFPlayer_Mini1.GND#6, VCC1.-, Part1.GND
  N2: U1.Pin_5, Part1.Trig
  N3: U1.Pin_6, Part1.Echo
  N4: U1.Pin_7, DFPlayer_Mini1.IO_1
  VCC: U1.Pin_8, DFPlayer_Mini1.VCC, VCC1.+, Part1.VCC
  N5: DFPlayer_Mini1.SPK1, SP1.-
  N6: DFPlayer_Mini1.SPK2, SP1.+

custom parts:
  DFPlayer MINI: MP3 module by DFRobot.com for playing Music from an SD-Card. Supports WAV and MP3 files.
